# Fritzing sketch CubeSat Computer Design (saved by Fritzing 0.9.3b)
perfboards: 3

parts:
  Part1 = Arduino Uno (Rev3) - ICSP
  Part2 = Gas Sensor Breakout Board
  Part3 = Compass Module - HMC6352
  Part4 = Adafruit_BMP280
  TP1 = TP4056 [chip_label=TP4056 package="DIP (Dual Inline) [THT]"]
  JP1 = Header 2 [package=screwterminal-3.5mm-2_lock]  # not connected
  Part5 = Solar Cell
  LED1 = RGB LED - (4 legs) [package="5 mm [THT]"]
  J1 = Piezo Speaker
  Part6 = Gas Sensor Breakout Board
  Part7 = Gas Sensor Breakout Board
  DHT1 = DHT11 Humitidy and Temperature Sensor
  Part8 = NRF24L01+ Breakout Board
  M1 = Dagu DGServo 9g (Top view) [part_number=RS001B]
  M2 = Dagu DGServo 9g (Top view) [part_number=RS001B]
  Part9 = Solar Cell
  Part10 = Solar Cell
  Part11 = Solar Cell
  Part12 = ACS712 Low Current Sensor Board v12
  JP3 = Header 2 [package=molex-1x2_lock]
  JP2 = Header 2 [package=molex-1x2_lock]
  JP4 = Header 2 [package=molex-1x2_lock]
  R1 = Resistor [tolerance=±5% resistance=220 package="2010 [SMD]"]
  R2 = Resistor [tolerance=±5% resistance=220 package="2010 [SMD]"]
  VCC1 = 4 x AAA Battery Mount
  U1 = attiny85 [package=dip]  # not connected

nets:
  N1: Part1.A2, Part12.VO
  N2: Part1.A3, Part12.IP+, R1.Pin_1
  N3: Part1.ICSP_MISO, Part1.D12/MISO, Part3.SDA, Part4.SDI/SDA
  5V: Part1.5V, Part8.VCC, Part12.5V
  GND: Part1.GND, Part3.GND, Part4.GND, TP1.pin6, LED1.common_anode, J1.pin1, M1.gnd, M2.gnd, Part12.GND, R2.Pin_1
  N4: Part1.A5/SCL, Part3.SCL, Part4.SDO/ADR
  3V3: Part1.3V3, Part3.VCC, Part4.VIN
  N5: Part2.A1, JP2.1
  N6: Part2.H1, Part6.H1, DHT1.VDD
  GND_2: Part2.GND, Part7.GND, DHT1.GND, JP4.1
  N7: TP1.pin1, Part10.-
  N8: TP1.pin2, Part11.+
  N9: TP1.pin4, VCC1.+
  N10: TP1.pin5, VCC1.-
  N11: Part5.+, Part11.-
  N12: Part5.-, Part9.+
  N13: Part6.A1, JP2.2
  N14: Part7.A1, JP3.1
  N15: DHT1.DATA, JP3.2
  VCC: M1.vcc, M2.vcc
  N16: Part9.-, Part10.+

notes:
  What should i check ? Bat or Op Voltage?

custom parts:
  Adafruit_BMP280: Bosch has stepped up their game with their new BMP280 sensor, an environmental sensor with temperature, barometric pressure that is the next generation upgrade to the BMP085/BMP180/BMP183. This sensor is great for all sorts of weather sensing and can even be used in both I2C and SPI! This precision sensor from Bosch is the best low-cost, precision sensing solution for measuring barometric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
  TP4056: A DIP stand-in part for whatever IC you want. With 6 pins on a 300mil dual inline package (DIP) footprint.
  DHT11 Humitidy and Temperature Sensor: DHT11 Humidity and Temperature Sensor
