# Fritzing sketch Lander Computer (saved by Fritzing 0.9.3b)
perfboards: 1

parts:
  Part1 = Arduino Uno (Rev3)
  U1 = RELAY [package=relay-jzc]
  Part2 = InvenSense MPU6050
  Part3 = NRF24L01+ Breakout Board
  M2 = Dagu DGServo 9g (Top view) [part_number=RS001B]
  M3 = Dagu DGServo 9g (Top view) [part_number=RS001B]
  M4 = Dagu DGServo 9g (Top view) [part_number=RS001B]
  hc-sr1 = hc-sr04
  LED1 = LED - 5mm [color="Red (633nm)" package="5 mm [THT]"]
  LED2 = RGB LED (com. cathode, rgb) [package="5 mm [THT]"]
  JP1 = Header 2 [package=screwterminal-3.5mm-2_lock]
  BAT1 = Battery Holders [package=battery-aa-kit]
  BAT2 = Battery Holders [package=battery-aa-kit]
  J1 = Piezo Speaker  # not connected

nets:
  N1: Part1.A2, LED2.red_anode
  N2: Part1.A3, LED2.blue_anode
  N3: Part1.D8, Part3.CE
  N4: Part1.D9_PWM, hc-sr1.Echo
  N5: Part1.D11_PWM/MOSI, Part3.MOSI
  N6: Part1.D12/MISO, Part3.MISO
  N7: Part1.D13/SCK, Part3.SCK
  GND: Part1.GND, U1.COIL2, Part2.GND, Part3.GND, M2.gnd, hc-sr1.GND, LED2.common_cathode
  N8: Part1.A4/SDA, Part2.SDA
  N9: Part1.A5/SCL, Part2.SCL
  N10: Part1.D0/RX, LED2.green_anode
  N11: Part1.D1/TX, U1.NC
  N12: Part1.D2, Part2.INT
  N13: Part1.D3_PWM, M2.pulse
  N14: Part1.D4, hc-sr1.Trig
  N15: Part1.D5_PWM, M3.pulse
  N16: Part1.D6_PWM, M4.pulse
  N17: Part1.D7, Part3.CS
  VCC: Part1.5V, U1.COIL1, Part2.VCC, Part3.VCC, M2.vcc
  N18: U1.NO, LED1.cathode
  N19: U1.MAIN, LED1.anode
  GND_2: M3.gnd, M4.gnd, JP1.2, BAT2.-
  VCC_2: M3.vcc, M4.vcc, JP1.1, BAT1.+
